# Fritzing sketch Diagrama (saved by Fritzing 0.9.3b)
breadboards: 1

parts:
  Ethernet_shield = Arduino Ethernet Shield (Rev3)
  Arduino_Nano = Arduino Nano (Rev3.0)
  Sensor_de_sonido = Breakout Board for Electret Microphone
  LED28 = LEDs [package=led10mm]
  J1 = screw terminal, 3 pins
  J21 = female pin header, 3 pins [form="♀ (female)"]

nets:
  5V: Ethernet_shield.5V, Arduino_Nano.5V, Sensor_de_sonido.VCC, J21.pin1
  N1: Ethernet_shield.ETH_CS, Arduino_Nano.D10
  N2: Ethernet_shield.PWM_D11, Arduino_Nano.D11/MOSI
  N3: Ethernet_shield.SPI/D12, Arduino_Nano.D12/MISO
  N4: Ethernet_shield.SPI/D13, Arduino_Nano.D13/SCK
  GND: Ethernet_shield.GND, Arduino_Nano.D1/TX, Arduino_Nano.GND, Sensor_de_sonido.GND, J21.pin2
  N5: Arduino_Nano.D3, Sensor_de_sonido.AUD
  N6: Arduino_Nano.D4, J21.pin3
  N7: LED28.C, J1.pin1

notes:
  Modulo Relevador
  -Vcc -NC
  -GND -COM
  -IN -NO
  VCA 125

custom parts:
  LEDs: LEDs Standard schematic elements and footprints for 5mm, 3mm, 1206, and 0603 sized LEDs. 5mm - Spark Fun Electronics SKU : COM-00529 (and others)
